// Logisim project alu.circ as structural Verilog: 5 circuits, main circuit 1bit_adder
module _1bit_adder (
  input  A,
  input  B,
  input  Cin,
  output S,
  output Cout
);

  wire and_1_out, and_2_out, xor_1_out;

  xor xor_1 (xor_1_out, A, B);
  xor xor_2 (S, xor_1_out, Cin);
  and and_1 (and_1_out, xor_1_out, Cin);
  and and_2 (and_2_out, B, A);
  or or_1 (Cout, and_1_out, and_2_out);
endmodule

module _2bit_adder (
  input  [1:0] A,
  input  [1:0] B,
  input  Cin,
  output [1:0] S,
  output Cout
);

  wire n1bit_adder_1_cout;

  _1bit_adder u_1bit_adder_1 (.A(A[0]), .B(B[0]), .Cin(Cin), .Cout(n1bit_adder_1_cout), .S(S[0]));
  _1bit_adder u_1bit_adder_2 (.A(A[1]), .B(B[1]), .Cin(n1bit_adder_1_cout), .Cout(Cout), .S(S[1]));
endmodule

module _4bit_adder (
  input  [3:0] A,
  input  [3:0] B,
  output [3:0] S
);

  wire n2bit_adder_1_cout;

  _2bit_adder u_2bit_adder_1 (.A(A[1:0]), .B(B[1:0]), .Cin(1'b0), .Cout(n2bit_adder_1_cout), .S(S[1:0]));
  _2bit_adder u_2bit_adder_2 (.A(A[3:2]), .B(B[3:2]), .Cin(n2bit_adder_1_cout), .S(S[3:2]));  // open: Cout
endmodule

module _4_bit_sub (
  input  [3:0] in_1,
  input  [3:0] in_2,
  output [3:0] out_3
);

  wire [3:0] n4bit_adder_1_s, not_1_out;

  not not_1 (not_1_out[0], in_2[0]);
  not not_2 (not_1_out[1], in_2[1]);
  not not_3 (not_1_out[2], in_2[2]);
  not not_4 (not_1_out[3], in_2[3]);
  _4bit_adder u_4bit_adder_1 (.A(not_1_out), .B(4'b0001), .S(n4bit_adder_1_s));
  _4bit_adder u_4bit_adder_2 (.A(in_1), .B(n4bit_adder_1_s), .S(out_3));
endmodule

module alu (
  input  [3:0] A,
  input  [3:0] B,
  input  [1:0] ALUOp,
  output [3:0] C
);

  wire [3:0] and_1_out, n4_bit_sub_1_out_3, n4bit_adder_1_s, or_1_out;

  _4bit_adder u_4bit_adder_1 (.A(A), .B(B), .S(n4bit_adder_1_s));
  _4_bit_sub u_4_bit_sub_1 (.in_1(A), .in_2(B), .out_3(n4_bit_sub_1_out_3));
  assign and_1_out = A & B;  // AND_Gate and_1, 4 bits wide
  assign or_1_out = A | B;  // OR_Gate or_1, 4 bits wide
  Multiplexer #(.select(2), .width(4), .enable("false")) multiplexer_1 (
    .in0(n4bit_adder_1_s), .in1(n4_bit_sub_1_out_3), .in2(and_1_out), .in3(or_1_out), .out(C), .sel(ALUOp));
endmodule
