// Logisim project comparator.circ as structural Verilog: 2 circuits, main circuit 1bit_comp
module _1bit_comp (
  input  A,
  input  B,
  output Out,
  output Eql
);

  wire and_2_out, and_3_out, not_1_out, not_2_out, not_3_out;

  not not_1 (not_1_out, B);
  not not_2 (not_2_out, A);
  not not_3 (not_3_out, B);
  and and_1 (Out, A, not_1_out);
  and and_2 (and_2_out, not_2_out, not_3_out);
  and and_3 (and_3_out, A, B);
  or or_1 (Eql, and_2_out, and_3_out);
endmodule

module comparator (
  input  [3:0] A,
  input  [3:0] B,
  output Out
);

  wire and_1_out, and_2_out, and_3_out, n1bit_comp_1_eql, n1bit_comp_1_out, n1bit_comp_2_eql,
       n1bit_comp_2_out, n1bit_comp_3_eql, n1bit_comp_3_out, n1bit_comp_4_out;

  _1bit_comp u_1bit_comp_1 (.A(A[3]), .B(B[3]), .Out(n1bit_comp_1_out), .Eql(n1bit_comp_1_eql));
  _1bit_comp u_1bit_comp_2 (.A(A[2]), .B(B[2]), .Out(n1bit_comp_2_out), .Eql(n1bit_comp_2_eql));
  _1bit_comp u_1bit_comp_3 (.A(A[1]), .B(B[1]), .Out(n1bit_comp_3_out), .Eql(n1bit_comp_3_eql));
  _1bit_comp u_1bit_comp_4 (.A(A[0]), .B(B[0]), .Out(n1bit_comp_4_out));  // open: Eql
  and and_1 (and_1_out, n1bit_comp_1_eql, n1bit_comp_2_out);
  and and_2 (and_2_out, n1bit_comp_1_eql, n1bit_comp_2_eql, n1bit_comp_3_out);
  and and_3 (and_3_out, n1bit_comp_1_eql, n1bit_comp_2_eql, n1bit_comp_3_eql, n1bit_comp_4_out);
  or or_1 (Out, n1bit_comp_1_out, and_1_out, and_2_out, and_3_out);

  // Other names for the same wires on the sheet: In_1_0 = A[0]; In_1_1 = A[1]; In_1_2 = A[2]; In_1_3 = A[3];
  //   In_2_0 = B[0]; In_2_1 = B[1]; In_2_2 = B[2]; In_2_3 = B[3]
endmodule
