// Logisim project code.circ as structural Verilog: 1 circuit, main circuit fsm
module fsm (
  input  Clr,
  input  X,
  output Z
);

  wire and_1_out, and_2_out, clock_1_out, not_1_out, not_2_out;
  wire [0:0] or_1_out;
  wire [1:0] register_1_q;

  and and_1 (and_1_out, register_1_q[1], not_1_out);
  not not_1 (not_1_out, X);
  and and_2 (and_2_out, register_1_q[0], not_2_out, X);
  not not_2 (not_2_out, register_1_q[1]);
  or or_1 (or_1_out[0], and_1_out, and_2_out);
  Clock clock_1 (.out(clock_1_out));
  Register #(.width(2)) register_1 (.D({X, or_1_out[0]}), .Q(register_1_q), .clk(clock_1_out), .clr(Clr));  // open: en
  and and_3 (Z, or_1_out[0], X);
endmodule
