// Logisim project CPU.circ as structural Verilog: 6 circuits, main circuit main
module main (
  input  Reset,
  output [31:0] Instr,
  output RegWrite,
  output [4:0] RegAddr,
  output [31:0] RegData,
  output MemWrite,
  output [4:0] MemAddr,
  output [31:0] MemData
);

  wire alu_1_zero, and_1_out, Clk, controller_1_alusrc, controller_1_branch, controller_1_jump,
       controller_1_memtoreg, controller_1_regdst;
  wire [1:0] controller_1_extop;
  wire [2:0] controller_1_aluop;
  wire [31:0] alu_1_aluresult, ext_1_ext_out, grf_1_rd1, multiplexer_2_out, ram_1_data;

  Clock clock_1 (.out(Clk));
  IFU ifu_1 (.Instr(Instr), .Branch(and_1_out), .Clk(Clk), .Reset(Reset), .Addr(Instr[25:0]), .Jump(controller_1_jump));
  Controller controller_1 (
    .Op(Instr[31:26]), .Funct(Instr[5:0]), .Branch(controller_1_branch), .Jump(controller_1_jump),
    .MemtoReg(controller_1_memtoreg), .MemWrite(MemWrite), .ALUOp(controller_1_aluop),
    .ExtOp(controller_1_extop), .RegWrite(RegWrite), .RegDst(controller_1_regdst),
    .ALUSrc(controller_1_alusrc));
  Multiplexer #(.width(5), .enable("false")) multiplexer_1 (
    .in0(Instr[20:16]), .in1(Instr[15:11]), .out(RegAddr), .sel(controller_1_regdst));
  and and_1 (and_1_out, alu_1_zero, controller_1_branch);
  GRF grf_1 (
    .A1(Instr[25:21]), .A2(Instr[20:16]), .A3(RegAddr), .WD(RegData), .RD1(grf_1_rd1), .RD2(MemData),
    .WE(RegWrite), .CLK(Clk));
  EXT ext_1 (.Ext_In(Instr[15:0]), .Ext_Out(ext_1_ext_out), .ExtOp(controller_1_extop));
  ALU alu_1 (
    .SrcA(grf_1_rd1), .SrcB(multiplexer_2_out),
    .ALUResult({alu_1_aluresult[31:7], MemAddr, alu_1_aluresult[1:0]}), .ALUOp(controller_1_aluop),
    .Zero(alu_1_zero));
  Multiplexer #(.width(32), .enable("false")) multiplexer_2 (
    .in0(MemData), .in1(ext_1_ext_out), .out(multiplexer_2_out), .sel(controller_1_alusrc));
  RAM #(.addrWidth(5), .dataWidth(32), .bus("separate")) ram_1 (
    .addr(MemAddr), .din(MemData), .data(ram_1_data), .str(MemWrite), .clk(Clk));  // open: sel, ld, clr
  Multiplexer #(.width(32), .enable("false")) multiplexer_3 (
    .in0({alu_1_aluresult[31:7], MemAddr, alu_1_aluresult[1:0]}), .in1(ram_1_data), .out(RegData),
    .sel(controller_1_memtoreg));
endmodule

module GRF (
  input  [4:0] A1,
  input  WE,
  input  [4:0] A2,
  input  [4:0] A3,
  input  [31:0] WD,
  input  CLK,
  output [31:0] RD1,
  output [31:0] RD2
);

  wire En01, En02, En03, En04, En05, En06, En07, En08, En09, En10, En11, En12, En13, En14, En15, En16, En17,
       En18, En19, En20, En21, En22, En23, En24, En25, En26, En27, En28, En29, En30, En31;
  wire [30:0] bit_extender_1_out, decoder_1_out1;
  wire [31:0] O_01, O_02, O_03, O_04, O_05, O_06, O_07, O_08, O_09, O_10, O_11, O_12, O_13, O_14, O_15, O_16,
       O_17, O_18, O_19, O_20, O_21, O_22, O_23, O_24, O_25, O_26, O_27, O_28, O_29, O_30, O_31;

  assign bit_extender_1_out = {{30{WE}}, WE};  // Bit_Extender bit_extender_1
  assign {En31, En30, En29, En28, En27, En26, En25, En24, En23, En22, En21, En20, En19, En18, En17, En16, En15, En14, En13, En12, En11, En10, En09, En08, En07, En06, En05, En04, En03, En02, En01} = bit_extender_1_out & decoder_1_out1;  // AND_Gate and_1, 31 bits wide
  Decoder #(.select(5), .enable("false")) decoder_1 (
    .out1(decoder_1_out1[0]), .out2(decoder_1_out1[1]), .out3(decoder_1_out1[2]), .out4(decoder_1_out1[3]),
    .out5(decoder_1_out1[4]), .out6(decoder_1_out1[5]), .out7(decoder_1_out1[6]), .out8(decoder_1_out1[7]),
    .out9(decoder_1_out1[8]), .out10(decoder_1_out1[9]), .out11(decoder_1_out1[10]),
    .out12(decoder_1_out1[11]), .out13(decoder_1_out1[12]), .out14(decoder_1_out1[13]),
    .out15(decoder_1_out1[14]), .out16(decoder_1_out1[15]), .out17(decoder_1_out1[16]),
    .out18(decoder_1_out1[17]), .out19(decoder_1_out1[18]), .out20(decoder_1_out1[19]),
    .out21(decoder_1_out1[20]), .out22(decoder_1_out1[21]), .out23(decoder_1_out1[22]),
    .out24(decoder_1_out1[23]), .out25(decoder_1_out1[24]), .out26(decoder_1_out1[25]),
    .out27(decoder_1_out1[26]), .out28(decoder_1_out1[27]), .out29(decoder_1_out1[28]),
    .out30(decoder_1_out1[29]), .out31(decoder_1_out1[30]), .sel(A3));  // open: out0
  Register #(.width(32)) register_1 (.D(WD), .en(En01), .Q(O_01), .clk(CLK));  // open: clr
  Register #(.width(32)) register_2 (.D(WD), .en(En05), .Q(O_05), .clk(CLK));  // open: clr
  Register #(.width(32)) register_3 (.D(WD), .en(En09), .Q(O_09), .clk(CLK));  // open: clr
  Register #(.width(32)) register_4 (.D(WD), .en(En13), .Q(O_13), .clk(CLK));  // open: clr
  Register #(.width(32)) register_5 (.D(WD), .en(En17), .Q(O_17), .clk(CLK));  // open: clr
  Register #(.width(32)) register_6 (.D(WD), .en(En21), .Q(O_21), .clk(CLK));  // open: clr
  Register #(.width(32)) register_7 (.D(WD), .en(En25), .Q(O_25), .clk(CLK));  // open: clr
  Register #(.width(32)) register_8 (.D(WD), .en(En29), .Q(O_29), .clk(CLK));  // open: clr
  Register #(.width(32)) register_9 (.D(WD), .en(En02), .Q(O_02), .clk(CLK));  // open: clr
  Register #(.width(32)) register_10 (.D(WD), .en(En06), .Q(O_06), .clk(CLK));  // open: clr
  Register #(.width(32)) register_11 (.D(WD), .en(En10), .Q(O_10), .clk(CLK));  // open: clr
  Register #(.width(32)) register_12 (.D(WD), .en(En14), .Q(O_14), .clk(CLK));  // open: clr
  Register #(.width(32)) register_13 (.D(WD), .en(En18), .Q(O_18), .clk(CLK));  // open: clr
  Register #(.width(32)) register_14 (.D(WD), .en(En22), .Q(O_22), .clk(CLK));  // open: clr
  Register #(.width(32)) register_15 (.D(WD), .en(En26), .Q(O_26), .clk(CLK));  // open: clr
  Register #(.width(32)) register_16 (.D(WD), .en(En30), .Q(O_30), .clk(CLK));  // open: clr
  Register #(.width(32)) register_17 (.D(WD), .en(En03), .Q(O_03), .clk(CLK));  // open: clr
  Register #(.width(32)) register_18 (.D(WD), .en(En07), .Q(O_07), .clk(CLK));  // open: clr
  Register #(.width(32)) register_19 (.D(WD), .en(En11), .Q(O_11), .clk(CLK));  // open: clr
  Register #(.width(32)) register_20 (.D(WD), .en(En15), .Q(O_15), .clk(CLK));  // open: clr
  Register #(.width(32)) register_21 (.D(WD), .en(En19), .Q(O_19), .clk(CLK));  // open: clr
  Register #(.width(32)) register_22 (.D(WD), .en(En23), .Q(O_23), .clk(CLK));  // open: clr
  Register #(.width(32)) register_23 (.D(WD), .en(En27), .Q(O_27), .clk(CLK));  // open: clr
  Register #(.width(32)) register_24 (.D(WD), .en(En31), .Q(O_31), .clk(CLK));  // open: clr
  Register #(.width(32)) register_25 (.D(WD), .en(En04), .Q(O_04), .clk(CLK));  // open: clr
  Register #(.width(32)) register_26 (.D(WD), .en(En08), .Q(O_08), .clk(CLK));  // open: clr
  Register #(.width(32)) register_27 (.D(WD), .en(En12), .Q(O_12), .clk(CLK));  // open: clr
  Register #(.width(32)) register_28 (.D(WD), .en(En16), .Q(O_16), .clk(CLK));  // open: clr
  Register #(.width(32)) register_29 (.D(WD), .en(En20), .Q(O_20), .clk(CLK));  // open: clr
  Register #(.width(32)) register_30 (.D(WD), .en(En24), .Q(O_24), .clk(CLK));  // open: clr
  Register #(.width(32)) register_31 (.D(WD), .en(En28), .Q(O_28), .clk(CLK));  // open: clr
  Multiplexer #(.select(5), .width(32), .enable("false")) multiplexer_1 (
    .in0({32{1'b0}}), .in1(O_01), .in2(O_02), .in3(O_03), .in4(O_04), .in5(O_05), .in6(O_06), .in7(O_07),
    .in8(O_08), .in9(O_09), .in10(O_10), .in11(O_11), .in12(O_12), .in13(O_13), .in14(O_14), .in15(O_15),
    .in16(O_16), .in17(O_17), .in18(O_18), .in19(O_19), .in20(O_20), .in21(O_21), .in22(O_22), .in23(O_23),
    .in24(O_24), .in25(O_25), .in26(O_26), .in27(O_27), .in28(O_28), .in29(O_29), .in30(O_30), .in31(O_31),
    .out(RD1), .sel(A1));
  Multiplexer #(.select(5), .width(32), .enable("false")) multiplexer_2 (
    .in0({32{1'b0}}), .in1(O_01), .in2(O_02), .in3(O_03), .in4(O_04), .in5(O_05), .in6(O_06), .in7(O_07),
    .in8(O_08), .in9(O_09), .in10(O_10), .in11(O_11), .in12(O_12), .in13(O_13), .in14(O_14), .in15(O_15),
    .in16(O_16), .in17(O_17), .in18(O_18), .in19(O_19), .in20(O_20), .in21(O_21), .in22(O_22), .in23(O_23),
    .in24(O_24), .in25(O_25), .in26(O_26), .in27(O_27), .in28(O_28), .in29(O_29), .in30(O_30), .in31(O_31),
    .out(RD2), .sel(A2));
endmodule

module ALU (
  input  [2:0] ALUOp,
  input  [31:0] SrcA,
  input  [31:0] SrcB,
  output Zero,
  output [31:0] ALUResult
);

  wire or_2_out;
  wire [31:0] adder_1_out, and_1_out, bit_extender_1_out, multiplexer_1_out, not_1_out, or_1_out;

  assign not_1_out = ~SrcB;  // NOT_Gate not_1, 32 bits wide
  Multiplexer #(.width(32), .enable("false")) multiplexer_1 (
    .in0(SrcB), .in1(not_1_out), .out(multiplexer_1_out), .sel(ALUOp[2]));
  Adder #(.width(32)) adder_1 (.a(SrcA), .b(multiplexer_1_out), .out(adder_1_out), .cin(ALUOp[2]));  // open: cout
  assign and_1_out = SrcA & multiplexer_1_out;  // AND_Gate and_1, 32 bits wide
  assign or_1_out = SrcA | multiplexer_1_out;  // OR_Gate or_1, 32 bits wide
  assign bit_extender_1_out = {{31{1'b0}}, adder_1_out[31]};  // Bit_Extender bit_extender_1
  Multiplexer #(.select(2), .width(32), .enable("false")) multiplexer_2 (
    .in0(adder_1_out), .in1(and_1_out), .in2(or_1_out), .in3(bit_extender_1_out), .out(ALUResult),
    .sel(ALUOp[1:0]));
  or or_2 (or_2_out, ALUResult[0], ALUResult[1], ALUResult[2], ALUResult[3], ALUResult[4], ALUResult[5], ALUResult[6], ALUResult[7], ALUResult[8], ALUResult[9], ALUResult[10], ALUResult[11], ALUResult[12], ALUResult[13], ALUResult[14], ALUResult[15], ALUResult[16], ALUResult[17], ALUResult[18], ALUResult[19], ALUResult[20], ALUResult[21], ALUResult[22], ALUResult[23], ALUResult[24], ALUResult[25], ALUResult[26], ALUResult[27], ALUResult[28], ALUResult[29], ALUResult[30], ALUResult[31]);
  not not_2 (Zero, or_2_out);
endmodule

module EXT (
  input  [1:0] ExtOp,
  input  [15:0] Ext_In,
  output [31:0] Ext_Out
);

  wire [31:0] bit_extender_1_out, bit_extender_2_out;

  assign bit_extender_1_out = {{16{Ext_In[15]}}, Ext_In};  // Bit_Extender bit_extender_1
  assign bit_extender_2_out = {{16{1'b0}}, Ext_In};  // Bit_Extender bit_extender_2
  Multiplexer #(.select(2), .width(32), .enable("false")) multiplexer_1 (
    .in0(bit_extender_1_out), .in1(bit_extender_2_out),
    .in2({bit_extender_2_out[15:0], bit_extender_2_out[31:16]}), .out(Ext_Out), .sel(ExtOp));  // open: in3
endmodule

module IFU (
  input  Branch,
  input  Jump,
  input  Clk,
  input  Reset,
  input  [25:0] Addr,
  output [31:0] Instr
);

  wire [31:0] adder_1_out, adder_2_out, bit_extender_1_out, multiplexer_1_out, multiplexer_2_out, PC_q,
       shifter_1_out;

  assign bit_extender_1_out = {{16{Addr[15]}}, Addr[15:0]};  // Bit_Extender bit_extender_1
  Adder #(.width(32)) adder_1 (.a(PC_q), .b(32'h4), .out(adder_1_out));  // open: cin, cout
  Shifter #(.width(32)) shifter_1 (.in(bit_extender_1_out), .\dist (5'b00010), .out(shifter_1_out));
  Adder #(.width(32)) adder_2 (.a(adder_1_out), .b(shifter_1_out), .out(adder_2_out));  // open: cin, cout
  Multiplexer #(.width(32), .enable("false")) multiplexer_1 (
    .in0(adder_1_out), .in1(adder_2_out), .out(multiplexer_1_out), .sel(Branch));
  Multiplexer #(.width(32), .enable("false")) multiplexer_2 (
    .in0(multiplexer_1_out), .in1({adder_1_out[31:28], Addr, 2'b00}), .out(multiplexer_2_out), .sel(Jump));
  Register #(.width(32)) PC (.D(multiplexer_2_out), .Q(PC_q), .clk(Clk), .clr(Reset));  // open: en
  ROM #(.addrWidth(5), .dataWidth(32)) rom_1 (.addr(PC_q[6:2]), .data(Instr));  // open: sel
endmodule

module Controller (
  input  [5:0] Op,
  input  [5:0] Funct,
  output Branch,
  output Jump,
  output MemtoReg,
  output MemWrite,
  output [2:0] ALUOp,
  output ALUSrc,
  output [1:0] ExtOp,
  output RegWrite,
  output RegDst
);

  wire addu, not_1_out, not_2_out, not_3_out, not_4_out, not_5_out, not_6_out, not_7_out, not_8_out,
       not_9_out, not_10_out, not_11_out, not_12_out, R_out, subu;

  not not_1 (not_1_out, Op[5]);
  not not_2 (not_2_out, Funct[5]);
  not not_3 (not_3_out, Op[2]);
  not not_4 (not_4_out, Op[4]);
  not not_5 (not_5_out, Op[1]);
  not not_6 (not_6_out, Op[3]);
  not not_7 (not_7_out, Funct[4]);
  not not_8 (not_8_out, Funct[3]);
  not not_9 (not_9_out, Funct[2]);
  not not_10 (not_10_out, Funct[1]);
  not not_11 (not_11_out, Op[0]);
  not not_12 (not_12_out, Funct[0]);
  and ori (ExtOp[0], Op[0], not_5_out, Op[2], Op[3], not_4_out, not_1_out);
  and lw (MemtoReg, Op[0], Op[1], not_3_out, not_6_out, not_4_out, Op[5]);
  and sw (MemWrite, Op[0], Op[1], not_3_out, Op[3], not_4_out, Op[5]);
  and beq (Branch, not_11_out, not_5_out, Op[2], not_6_out, not_4_out, not_1_out);
  and lui (ExtOp[1], Op[0], Op[1], Op[2], Op[3], not_4_out, not_1_out);
  and R (R_out, not_11_out, not_5_out, not_3_out, not_6_out, not_4_out, not_1_out);
  and u_addu (addu, R_out, Funct[0], not_10_out, not_9_out, not_8_out, not_7_out, Funct[5]);
  and u_subu (subu, R_out, Funct[0], Funct[1], not_9_out, not_8_out, not_7_out, Funct[5]);
  or _1 (ALUOp[1], ExtOp[0], ExtOp[1]);
  or _2 (ALUOp[2], subu, Branch);
  or or_1 (ALUSrc, ExtOp[0], MemtoReg, MemWrite, ExtOp[1]);
  or or_2 (RegWrite, addu, subu, ExtOp[0], MemtoReg, ExtOp[1]);
  or or_3 (RegDst, addu, subu);

  assign ALUOp[0] = 1'b0;
  assign Jump = 1'b0;

  // Other names for the same wires on the sheet: beq = Branch; ori = ExtOp[0]; lui = ExtOp[1]; lw = MemtoReg;
  //   sw = MemWrite
endmodule
